# Fritzing sketch wheresleyclockdiagram (saved by Fritzing 0.9.6b)
circuit board: 12.9866cm x 7.08231cm
perfboards: 1

parts:
  Gizwits_WiFi_Witty_ESP-12F1 = Gizwits WiFi Witty ESP-12F
  JP2 = Header 4 [package=screwterminal-3.5mm-4_lock]
  JP3 = Header 4 [package=screwterminal-3.5mm-4_lock]
  JP4 = Header 4 [package=screwterminal-3.5mm-4_lock]
  X1 = USB Connectors [package=usb-a-s-nosilk-female]
  R1 = Resistor [tolerance=±5% resistance=10k package="2512 [SMD]"]
  Part1 = Arduino Pro Mini (3.3V)
  Part2 = Arduino Pro Mini (3.3V)
  U1 = V_REG_LD1117VXX [package=78xxl]
  JP5 = Header 2 [package=jst-2-smd]
  JP6 = Header 2 [package=jst-2-smd]
  JP7 = Header 2 [package=jst-2-smd]
  JP8 = Header 2 [package=jst-2-smd]
  JP1 = Header 4 [package=screwterminal-3.5mm-4_lock]

nets:
  VCC: Gizwits_WiFi_Witty_ESP-12F1.VCC, R1.Pin_0, Part1.VCC, Part2.VCC, U1.OUT
  GND: Gizwits_WiFi_Witty_ESP-12F1.GND, X1.GND, Part1.GND, Part2.GND, U1.GND, JP5.2, JP6.2, JP7.2, JP8.2
  N1: Gizwits_WiFi_Witty_ESP-12F1.GPIO0, R1.Pin_1
  N2: JP2.1, Part1.D4
  N3: JP2.2, Part1.D5
  N4: JP2.3, Part1.D6
  N5: JP2.4, Part1.D7
  N6: JP3.1, Part2.D4
  N7: JP3.2, Part2.D5
  N8: JP3.3, Part2.D6
  N9: JP3.4, Part2.D7
  N10: JP4.1, Part2.D8
  N11: JP4.2, Part2.D9
  N12: JP4.3, Part2.D10
  N13: JP4.4, Part2.MOSI
  N14: X1.VBUS, U1.IN, JP5.1, JP6.1, JP7.1, JP8.1
  N15: Part1.A4, Part2.A4
  N16: Part1.A5, Part2.A5
  N17: Part1.MOSI, JP1.4
  N18: Part1.D10, JP1.3
  N19: Part1.D9, JP1.2
  N20: Part1.D8, JP1.1
