# Fritzing sketch wheresleyclockdiagram3 (saved by Fritzing 0.9.6b)
perfboards: 1

parts:
  R3 = Resistor [tolerance=±5% resistance=10k package="2512 [SMD]"]
  U3 = V_REG_LD1117VXX [package=78xxl]
  Gizwits_WiFi_Witty_ESP-12F3 = Gizwits WiFi Witty ESP-12F
  Part6 = Arduino Pro Mini (3.3V)
  Part7 = Arduino Pro Mini (3.3V)
  Part8 = Adafruit Micro USB Breakout [part_number="Adafruit #1833"]
  Driver1 = 28BYJ-48 Driver Module [part_number=ULN2003 package=THT]
  Driver2 = 28BYJ-48 Driver Module [part_number=ULN2003 package=THT]
  Driver3 = 28BYJ-48 Driver Module [part_number=ULN2003 package=THT]
  Driver4 = 28BYJ-48 Driver Module [part_number=ULN2003 package=THT]
  SM1 = 28BYJ-48 Stepper Motor [part_number=28BYJ-48]
  SM2 = 28BYJ-48 Stepper Motor [part_number=28BYJ-48]  # not connected
  SM3 = 28BYJ-48 Stepper Motor [part_number=28BYJ-48]  # not connected
  SM4 = 28BYJ-48 Stepper Motor [part_number=28BYJ-48]  # not connected

nets:
  N1: R3.Pin_0, Gizwits_WiFi_Witty_ESP-12F3.GPIO0
  N2: R3.Pin_1, Gizwits_WiFi_Witty_ESP-12F3.VCC
  N3: U3.OUT, Part7.VCC
  GND: U3.GND, Gizwits_WiFi_Witty_ESP-12F3.GND, Part6.GND, Part7.GND, Part8.GND
  N4: U3.IN, Part8.VBUS
  N5: Part6.A4, Part7.A4
  N6: Part6.A5, Part7.A5
  N7: Part6.MOSI, Driver2.IN4
  N8: Part6.D10, Driver2.IN3
  N9: Part6.D9, Driver2.IN2
  N10: Part6.D8, Driver2.IN1
  N11: Part6.D7, Driver1.IN4
  N12: Part6.D6, Driver1.IN3
  N13: Part6.D5, Driver1.IN2
  N14: Part6.D4, Driver1.IN1
  N15: Part7.MOSI, Driver4.IN4
  N16: Part7.D10, Driver4.IN3
  N17: Part7.D9, Driver4.IN2
  N18: Part7.D8, Driver4.IN1
  N19: Part7.D7, Driver3.IN4
  N20: Part7.D6, Driver3.IN3
  N21: Part7.D5, Driver3.IN2
  N22: Part7.D4, Driver3.IN1
  N23: Driver2.blue-pin, SM1.blue-pin
  N24: Driver2.pink-pin, SM1.pink-pin
  N25: Driver2.yellow-pin, SM1.yellow-pin
  N26: Driver2.orange-pin, SM1.orange-pin
  N27: Driver2.red-pin, SM1.red-pin

custom parts:
  Adafruit Micro USB Breakout: Simple but effective - this breakout board has a USB Micro-B connector, with all 5 pins broken out. Great for pairing with a microcontroller with USB support, or adding USB 5V power to a project. We use a micro-AB connector with through-hole shielding pads for an excellent strong connection - it won't rip off by accident! Comes with one fully assembled and tested micro B breakout PCB and a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
  28BYJ-48 Driver Module: Generic male header
  28BYJ-48 Stepper Motor: Unipolar Stepper Motor 28BYJ-48 Top coil - pink & orange Bottom coil - blue & yellow Common rail - red Connector pins: blue - pink - yellow - orange - red
